// Logisim project week12.circ as structural Verilog: 1 circuit, main circuit main
module main (
  input  MemtoReg,
  input  MemWrite,
  input  in_3,
  input  ALUSrc,
  input  [2:0] in_5
);

  wire button_1_out, clock_1_out, main_2_p1, main_2_p5;
  wire [4:0] multiplexer_1_out, rom_1_data_2, rom_1_data_3;
  wire [5:0] rom_1_data;
  wire [7:0] adder_1_out, register_1_q;
  wire [31:0] bit_extender_1_out, main_1_rd1, main_1_rd2, main_2_p7, main_3_p5, multiplexer_3_out;
  wire [31:16] rom_1_data_4;

  Clock clock_1 (.out(clock_1_out));
  Button button_1 (.out(button_1_out));
  Register register_1 (.D(adder_1_out), .Q(register_1_q), .clk(clock_1_out), .clr(button_1_out));  // open: en
  Adder adder_1 (.a(register_1_q), .b(8'h4), .out(adder_1_out));  // open: cin, cout
  ROM #(.addrWidth(6), .dataWidth(32)) rom_1 (
    .addr(register_1_q[7:2]), .data({rom_1_data_4, rom_1_data_3, rom_1_data_2, rom_1_data}));  // open: sel
  // Probe on rom_1_data_4[20:16]
  // Probe on rom_1_data_4[31:26]
  assign bit_extender_1_out = {{16{rom_1_data_3[4]}}, {rom_1_data_3, rom_1_data_2, rom_1_data}};  // Bit_Extender bit_extender_1
  Multiplexer #(.width(5)) multiplexer_1 (
    .in0(rom_1_data_4[20:16]), .in1(rom_1_data_3), .out(multiplexer_1_out));  // open: sel, en
  RegFile_main main_1 (
    .A1(rom_1_data_4[25:21]), .in_2(clock_1_out), .A2(rom_1_data_4[20:16]), .A3(multiplexer_1_out),
    .WD3(multiplexer_3_out), .in_6(main_2_p1), .Rd1(main_1_rd1), .Rd2(main_1_rd2));
  Multiplexer #(.width(32)) multiplexer_2 (.in1(bit_extender_1_out), .out(main_1_rd2), .sel(ALUSrc));  // open: in0, en
  // Probe on main_1_rd1
  // ALU_design_main main_2: pin names not known; wires that end beside it: main_2_p1, in_3, main_1_rd1, main_1_rd2, main_2_p5, main_2_p5, main_2_p7, in_5
  // datamem_main main_3: pin names not known; wires that end beside it: main_2_p7[8:0], main_1_rd2, clock_1_out, MemWrite, main_3_p5
  Multiplexer #(.width(32)) multiplexer_3 (
    .in0(main_2_p7), .in1(main_3_p5), .out(multiplexer_3_out), .sel(MemtoReg));  // open: en

  // Notes on the sheet:
  //   20205274 허태훈
  //   RegFile 디자인 당시, Pin과 A2의 위 아래를 바꾸고 설계하여 
  //   위치가 변경되었습니다
  //   lw $t2, 32($0)
  //   contents of rom_1 (hex, n*v repeats v):
  //   8c010000 ac010004 14b4820
endmodule
