// Logisim project main_decoder.circ as structural Verilog: 1 circuit, main circuit main
module main (
  input  op5,
  input  op4,
  input  op3,
  input  op2,
  input  op1,
  input  op0,
  output RegWrite,
  output RegDst,
  output AluSrc,
  output Branch,
  output MemWrite,
  output MemToReg,
  output Jump,
  output ALUOp1,
  output ALUOp0
);

  wire and_1_out, and_2_out, not_1_out, not_2_out, not_3_out, not_5_out, not_6_out, not_7_out;

  not not_1 (not_1_out, op2);
  not not_2 (not_2_out, op1);
  not not_3 (not_3_out, op3);
  not not_4 (RegDst, op1);
  not not_5 (not_5_out, op0);
  not not_6 (not_6_out, op2);
  not not_7 (not_7_out, op1);
  and and_1 (and_1_out, not_1_out, not_2_out);
  and and_2 (and_2_out, op5, not_3_out);
  and and_3 (Jump, op1, not_5_out);
  and and_4 (ALUOp1, not_6_out, not_7_out);
  or or_1 (RegWrite, and_1_out, and_2_out);

  assign ALUOp0 = op2;
  assign AluSrc = op1;
  assign Branch = op2;
  assign MemToReg = op1;
  assign MemWrite = op3;
endmodule
