// Logisim project week14.circ as structural Verilog: 1 circuit, main circuit main
module main (
  input  MemtoReg,
  input  MemWrite,
  input  Jump,
  input  RegWrite,
  input  ALUSrc,
  input  [2:0] in_6,
  input  RegDst
);

  wire button_1_out, CLK_out, main_2_p1, main_2_p5;
  wire [4:0] multiplexer_3_out, rom_1_data_2;
  wire [7:0] adder_1_out, multiplexer_1_out, multiplexer_2_out, register_1_q;
  wire [15:0] rom_1_data;
  wire [27:0] bit_extender_3_out, shifter_2_out;
  wire [31:0] adder_2_out, bit_extender_1_out, bit_extender_2_out, main_1_rd1, main_1_rd2, main_2_p7,
       main_3_p5, main_3_p6, multiplexer_5_out, shifter_1_out;
  wire [31:21] rom_1_data_3;

  Clock CLK (.out(CLK_out));
  Multiplexer #(.width(8)) multiplexer_1 (
    .in0(adder_1_out), .in1(adder_2_out[7:0]), .out(multiplexer_1_out));  // open: sel, en
  Multiplexer #(.width(8)) multiplexer_2 (
    .in0(multiplexer_1_out), .in1(shifter_2_out[7:0]), .out(multiplexer_2_out), .sel(Jump));  // open: en
  Button button_1 (.out(button_1_out));
  Register register_1 (.D(multiplexer_2_out), .Q(register_1_q), .clk(CLK_out), .clr(button_1_out));  // open: en
  Adder adder_1 (.a(register_1_q), .b(8'h4), .out(adder_1_out));  // open: cin, cout
  assign bit_extender_1_out = {{24{adder_1_out[7]}}, adder_1_out};  // Bit_Extender bit_extender_1
  ROM #(.addrWidth(6), .dataWidth(32)) rom_1 (
    .addr(register_1_q[7:2]), .data({rom_1_data_3, rom_1_data_2, rom_1_data}));  // open: sel
  // Probe on rom_1_data_2
  // Probe on rom_1_data_3[31:26]
  assign bit_extender_2_out = {{16{rom_1_data[15]}}, rom_1_data};  // Bit_Extender bit_extender_2
  Multiplexer #(.width(5)) multiplexer_3 (
    .in0(rom_1_data_2), .in1(rom_1_data[15:11]), .out(multiplexer_3_out), .sel(RegDst));  // open: en
  RegFile_main main_1 (
    .A1(rom_1_data_3[25:21]), .in_2(CLK_out), .A2(rom_1_data_2), .A3(multiplexer_3_out),
    .WD3(multiplexer_5_out), .in_6(main_2_p1), .Rd1(main_1_rd1), .Rd2(main_1_rd2));
  Multiplexer #(.width(32)) multiplexer_4 (.in1(bit_extender_2_out), .out(main_1_rd2), .sel(ALUSrc));  // open: in0, en
  assign bit_extender_3_out = {{2{rom_1_data_3[25]}}, {rom_1_data_3[25:21], rom_1_data_2, rom_1_data}};  // Bit_Extender bit_extender_3
  // Probe on main_1_rd1
  Shifter #(.width(32)) shifter_1 (.in(bit_extender_2_out), .\dist (5'b00010), .out(shifter_1_out));
  Shifter #(.width(28)) shifter_2 (.in(bit_extender_3_out), .\dist (5'b00010), .out(shifter_2_out));
  // ALU_design_main main_2: pin names not known; wires that end beside it: main_2_p1, RegWrite, main_1_rd1, main_1_rd2, main_2_p5, main_2_p5, main_2_p7, in_6
  Adder #(.width(32)) adder_2 (.a(shifter_1_out), .b(bit_extender_1_out), .out(adder_2_out));  // open: cin, cout
  // datamem_main main_3: pin names not known; wires that end beside it: main_2_p7[8:0], main_1_rd2, CLK_out, MemWrite, main_3_p5, main_3_p6
  Multiplexer #(.width(32)) multiplexer_5 (
    .in0(main_2_p7), .in1(main_3_p5), .out(multiplexer_5_out), .sel(MemtoReg));  // open: en
  _7_Segment_Display u_7_segment_display_1 (
    .g(main_3_p6[7]), .f(main_3_p6[6]), .a(main_3_p6[0]), .b(main_3_p6[1]), .e(main_3_p6[5]),
    .d(main_3_p6[4]), .c(main_3_p6[3]), .dp(main_3_p6[2]));
  _7_Segment_Display u_7_segment_display_2 (
    .g(main_3_p6[15]), .f(main_3_p6[14]), .a(main_3_p6[8]), .b(main_3_p6[9]), .e(main_3_p6[13]),
    .d(main_3_p6[12]), .c(main_3_p6[11]), .dp(main_3_p6[10]));

  // Notes on the sheet:
  //   PC + 4
  //   lw $t2, 32($0)
  //   contents of rom_1 (hex, n*v repeats v):
  //   2001ffff ac010004 20030000 1041000
  //   20205274 허태훈
  //   offset << 2
  //   PC + 4 offset << 2
  //   Memory Mappied ID
  //   Memory Mappied ID
endmodule
