// Logisim project regfile16.circ as structural Verilog: 1 circuit, main circuit main
module main (
  input  [3:0] A1,
  input  [3:0] A2,
  input  CLK,
  input  WE,
  input  [3:0] A3,
  input  [31:0] WD3,
  output [31:0] RD1,
  output [31:0] RD2
);

  wire demultiplexer_1_out0, demultiplexer_1_out1, demultiplexer_1_out2, demultiplexer_1_out3;
  wire [31:0] demultiplexer_2_out0, demultiplexer_2_out1, demultiplexer_2_out2, demultiplexer_2_out3,
       main_1_out_7, main_1_out_8, main_2_out_7, main_2_out_8, main_3_out_7, main_3_out_8, main_4_out_7,
       main_4_out_8;

  Demultiplexer #(.select(2)) demultiplexer_1 (
    .out0(demultiplexer_1_out0), .out1(demultiplexer_1_out1), .out2(demultiplexer_1_out2),
    .out3(demultiplexer_1_out3), .in(WE), .sel(A3[3:2]));  // open: en
  Demultiplexer #(.select(2), .width(32)) demultiplexer_2 (
    .out0(demultiplexer_2_out0), .out1(demultiplexer_2_out1), .out2(demultiplexer_2_out2),
    .out3(demultiplexer_2_out3), .in(WD3), .sel(A3[3:2]));  // open: en
  regfile4_main main_1 (
    .A1(A1[1:0]), .A2(A2[1:0]), .WD3(demultiplexer_2_out0), .A3(A3[1:0]), .CLK(CLK), .out_7(main_1_out_7),
    .out_8(main_1_out_8), .WE(demultiplexer_1_out0));
  regfile4_main main_2 (
    .A1(A1[1:0]), .A2(A2[1:0]), .WD3(demultiplexer_2_out1), .A3(A3[1:0]), .CLK(CLK), .out_7(main_2_out_7),
    .out_8(main_2_out_8), .WE(demultiplexer_1_out1));
  regfile4_main main_3 (
    .A1(A1[1:0]), .A2(A2[1:0]), .WD3(demultiplexer_2_out2), .A3(A3[1:0]), .CLK(CLK), .out_7(main_3_out_7),
    .out_8(main_3_out_8), .WE(demultiplexer_1_out2));
  regfile4_main main_4 (
    .A1(A1[1:0]), .A2(A2[1:0]), .WD3(demultiplexer_2_out3), .A3(A3[1:0]), .CLK(CLK), .out_7(main_4_out_7),
    .out_8(main_4_out_8), .WE(demultiplexer_1_out3));
  Multiplexer #(.select(2), .width(32)) multiplexer_1 (
    .in0(main_1_out_7), .in1(main_2_out_7), .in2(main_3_out_7), .in3(main_4_out_7), .out(RD1), .sel(A1[3:2]));  // open: en
  Multiplexer #(.select(2), .width(32)) multiplexer_2 (
    .in0(main_1_out_8), .in1(main_2_out_8), .in2(main_3_out_8), .in3(main_4_out_8), .out(RD2), .sel(A2[3:2]));  // open: en
endmodule
